# Fritzing sketch pool - Copy (saved by Fritzing 0.9.2b)
circuit board: 11.4441cm x 6.95677cm
breadboards: 1

parts:
  SOLAR = Momentary Switch [package=tactile-pth]
  UP = Momentary Switch [package=tactile-pth]
  DOWN = Momentary Switch [package=tactile-pth]
  R2 = Resistor [tolerance=±5% resistance=470 package=THT]
  R3 = Resistor [tolerance=±5% resistance=1k package=THT]
  1602_I2C_LCD = Grove OLED 128x96
  Roof_Sensor = DS18B20 1-Wire Temperature Sensor [part_number=DS18B20]
  U25 = ESP8266 WiFi Module [part_number=ESP8266]
  R9 = Resistor [tolerance=±5% resistance=4.7k package=THT]
  Water_Sensor = DS18B20 1-Wire Temperature Sensor [part_number=DS18B20]
  U26 = RELAY-SOLIDSTATE [package=relay-s108t02]
  U27 = Vibration Motor- ROB-08449 [package=vibe-motor-10mm]
  C1 = Ceramic Capacitor [capacitance=0.1µF package="200 mil [THT, multilayer]"]
  C4 = Electrolytic Capacitor [capacitance=1mF package="100 mil [THT, electrolytic]"]
  Air_Sensor = DS18B20 1-Wire Temperature Sensor [part_number=DS18B20]
  PUMP = Momentary Switch [package=tactile-pth]
  R11 = Resistor [tolerance=±5% resistance=10k package=THT]
  Pressure = TRIMPOT [package=3386u]
  R1 = Resistor [tolerance=±5% resistance=4.7k package=THT]
  R2_1 = Resistor [tolerance=±5% resistance=1k package=THT]
  Q2 = NPN-Transistor [package="SOT-23 [SMD]"]
  R14 = Resistor [tolerance=±5% resistance=470 package=THT]
  R2_2 = Resistor [tolerance=±5% resistance=500 package=THT]
  U28 = MOC3031-M [package=dil06]
  U29 = TRIAC [package=to-92]
  R16 = Resistor [tolerance=±5% resistance=470 package=THT]
  Solar_On = Inductor [package="1206 [SMD]"]
  U30 = V18ZA2P [package=v18za2p]
  U31 = V18ZA2P [package=v18za2p]
  U32 = MOC3031-M [package=dil06]
  U33 = TRIAC [package=to-92]
  R18 = Resistor [tolerance=±5% resistance=470 package=THT]
  Solar_Off = Inductor [package="1206 [SMD]"]

nets:
  GND: SOLAR.1, SOLAR.2, UP.1, UP.2, DOWN.1, DOWN.2, 1602_I2C_LCD.GND, Roof_Sensor.GND, U25.GND, Water_Sensor.GND, U27.-, C1.0, C4.-, Air_Sensor.GND, PUMP.1, PUMP.2, Pressure.CCW, Q2.2, R2_2.Pin_1, U28.2, Solar_On.pin_1, U32.2, Solar_Off.pin_1
  N1: SOLAR.3, SOLAR.4, U25.GPIO_13
  N2: UP.3, UP.4, U25.GPIO_16, R11.Pin_0
  N3: DOWN.3, DOWN.4, U25.GPIO_5
  N4: R2.Pin_0, R3.Pin_0, U25.GPIO_15
  N5: R2.Pin_1, U28.1
  N6: R3.Pin_1, Q2.0
  5V: 1602_I2C_LCD.VCC, Pressure.CW
  N7: 1602_I2C_LCD.SDA, U25.GPIO_0
  N8: 1602_I2C_LCD.SCL, U25.GPIO_2
  3.3V: Roof_Sensor.VDD, U25.VCC, U25.CH_PD, U25.REST, R9.Pin_0, Water_Sensor.VDD, U26.+, C1.1, C4.+, Air_Sensor.VDD, R11.Pin_1, R14.Pin_0
  N9: Roof_Sensor.DQ, U25.GPIO_4, R9.Pin_1, Water_Sensor.DQ, Air_Sensor.DQ
  N10: U25.ADC_0, R1.Pin_0, R2_1.Pin_1
  N11: U25.GPIO_14, U26.-
  N12: U25.GPIO_12, PUMP.3, PUMP.4
  N13: U26.T1, U27.+
  240V: U26.T2
  N14: Pressure.WIPER, R1.Pin_1
  N15: R2_1.Pin_0, R2_2.Pin_0
  N16: Q2.1, R14.Pin_1, U32.1
  N17: U28.4, R16.Pin_0
  24V: U28.6, U29.M2, U30.P$2, U31.P$2, U32.6, U33.M2
  N18: U29.M1, Solar_On.pin_0, U30.P$1
  N19: U29.G, R16.Pin_1
  N20: U31.P$1, U33.M1, Solar_Off.pin_0
  N21: U32.4, R18.Pin_0
  N22: U33.G, R18.Pin_1

notes:
  pool valve:
  red-black
  white-black

custom parts:
  ESP8266 WiFi Module: Generic WiFi Module based on the ESP8266 with onboard PCB antenna and UART communications
