# Fritzing sketch pool (saved by Fritzing 0.9.4)
circuit board: 11.4441cm x 6.95677cm
breadboards: 1

parts:
  Solar_On = Inductor [package="1206 [SMD]"]
  SOLAR = Momentary Switch [package=tactile-pth]
  DOWN = Momentary Switch [package=tactile-pth]
  R2 = Resistor [tolerance=±5% resistance=1k package=THT]
  U6 = TRIAC [package=to-92]
  U12 = TRIAC [package=to-92]
  R3 = Resistor [tolerance=±5% resistance=1k package=THT]
  Solar_Off = Inductor [package="1206 [SMD]"]
  1602_I2C_LCD = Grove OLED 128x96
  U23 = V18ZA2P [package=v18za2p]
  U24 = V18ZA2P [package=v18za2p]
  Roof_Sensor = DS18B20 1-Wire Temperature Sensor [part_number=DS18B20]
  U25 = ESP8266 WiFi Module [part_number=ESP8266]
  R9 = Resistor [tolerance=±5% resistance=4.7k package=THT]
  Water_Sensor = DS18B20 1-Wire Temperature Sensor [part_number=DS18B20]
  Pool_Pump = Vibration Motor- ROB-08449 [package=vibe-motor-10mm]
  C1 = Ceramic Capacitor [capacitance=0.1µF package="200 mil [THT, multilayer]"]
  C4 = Electrolytic Capacitor [capacitance=1mF package="100 mil [THT, electrolytic]"]
  Air_Sensor = DS18B20 1-Wire Temperature Sensor [part_number=DS18B20]
  PUMP = Momentary Switch [package=tactile-pth]
  R11 = Resistor [tolerance=±5% resistance=10k package=THT]
  Pressure = TRIMPOT [package=3386u]
  R1 = Resistor [tolerance=±5% resistance=4.7k package=THT]
  R2_1 = Resistor [tolerance=±5% resistance=1k package=THT]
  Q2 = NPN-Transistor [package="SOT-23 [SMD]"]
  R14 = Resistor [tolerance=±5% resistance=330 package=THT]
  R2_2 = Resistor [tolerance=±5% resistance=500 package=THT]
  U26 = V18ZA2P [package=v18za2p]
  U27 = TRIAC [package=to-92]
  R15 = Resistor [tolerance=±5% resistance=1k package=THT]
  Pool_Pump_Relay = Inductor [package="1206 [SMD]"]
  S1 = Square Pushbutton
  S2 = Square Pushbutton
  Spa_Pump = Vibration Motor- ROB-08449 [package=vibe-motor-10mm]
  U30 = V18ZA2P [package=v18za2p]
  U31 = TRIAC [package=to-92]
  R16 = Resistor [tolerance=±5% resistance=1k package=THT]
  Spa_Pump_Relay = Inductor [package="1206 [SMD]"]
  S3 = Square Pushbutton
  S4 = Square Pushbutton
  SPA = Momentary Switch [package=tactile-pth]
  Spa_Sensor = DS18B20 1-Wire Temperature Sensor [part_number=DS18B20]
  U32 = PCF8574 [package="DIP16 [THT]"]
  Part1 = Adafruit ADS1115 16Bit I2C ADC [part_number="Adafruit #1085"]
  UP = Momentary Switch [package=tactile-pth]

nets (from the schematic view):
  N1: Solar_On.pin_0, U6.M2, U23.P$2
  24V: Solar_On.pin_1, Solar_Off.pin_1, Pool_Pump_Relay.pin_1, Spa_Pump_Relay.pin_1
  N2: SOLAR.1, SOLAR.2, U32.P2
  GND: SOLAR.3, SOLAR.4, DOWN.3, DOWN.4, U6.M1, U12.M1, 1602_I2C_LCD.GND, U23.P$1, U24.P$1, Roof_Sensor.GND, U25.GND, Water_Sensor.GND, C1.0, C4.-, Air_Sensor.GND, PUMP.3, PUMP.4, Pressure.CCW, Q2.2, R2_2.Pin_1, U26.P$1, U27.M1, U30.P$1, U31.M1, SPA.3, SPA.4, Spa_Sensor.GND, U32.A0, U32.A1, U32.A2, U32.GND, Part1.AIN3, Part1.AIN2, Part1.AIN1, Part1.ADDR, Part1.GND, UP.3, UP.4
  N3: DOWN.1, DOWN.2, U32.P4
  N4: R2.Pin_0, R3.Pin_0, U32.P7
  N5: R2.Pin_1, U6.G
  N6: U12.G, Q2.1, R14.Pin_1
  N7: U12.M2, Solar_Off.pin_0, U24.P$2
  N8: R3.Pin_1, Q2.0
  5V: 1602_I2C_LCD.VCC, Pressure.CW
  N9: 1602_I2C_LCD.SDA, U25.GPIO_0, U32.SCL, Part1.SCL
  N10: 1602_I2C_LCD.SCL, U25.GPIO_2, U32.SDA, Part1.SDA
  3.3V: Roof_Sensor.VDD, U25.VCC, U25.CH_PD, U25.REST, R9.Pin_0, Water_Sensor.VDD, C1.1, C4.+, Air_Sensor.VDD, R11.Pin_1, R14.Pin_0, Spa_Sensor.VDD, U32.VCC, Part1.VDD
  N11: Roof_Sensor.DQ, U25.GPIO_4, R9.Pin_1, Water_Sensor.DQ, Air_Sensor.DQ, Spa_Sensor.DQ
  N12: U25.GPIO_16, R11.Pin_0
  N13: Pool_Pump.+, S1.leg0
  N14: Pool_Pump.-, S2.leg0
  N15: PUMP.1, PUMP.2, U32.P1
  N16: Pressure.WIPER, R1.Pin_1
  N17: R1.Pin_0, R2_1.Pin_1, Part1.AIN0
  N18: R2_1.Pin_0, R2_2.Pin_0
  N19: U26.P$2, U27.M2, Pool_Pump_Relay.pin_0
  N20: U27.G, R15.Pin_1
  N21: R15.Pin_0, U32.P5
  240V: S1.leg1, S2.leg1, S3.leg1, S4.leg1
  N22: Spa_Pump.+, S3.leg0
  N23: Spa_Pump.-, S4.leg0
  N24: U30.P$2, U31.M2, Spa_Pump_Relay.pin_0
  N25: U31.G, R16.Pin_1
  N26: R16.Pin_0, U32.P6
  N27: SPA.1, SPA.2, U32.P0
  N28: U32.P3, UP.1, UP.2

notes:
  pool valve:
  red-black
  white-black
  pool light circuit?

custom parts:
  ESP8266 WiFi Module: Generic WiFi Module based on the ESP8266 with onboard PCB antenna and UART communications
  Adafruit ADS1115 16Bit I2C ADC: For microcontrollers without an analog-to-digital converter or when you want a higher-precision ADC, the ADS1115 provides 16-bit precision at 860 samples/second over I2C. The chip can be configured as 4 single-ended input channels, or two differential channels. As a nice bonus, it even includes a programmable gain amplifier, up to x16, to help boost up smaller single/differential signals to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
